# Fritzing sketch dan_spedenspelit_fritz_board (saved by Fritzing 0.9.3b)
breadboards: 1

parts:
  R1 = Resistor [tolerance=±5% resistance=220 package=THT]
  Part1 = Arduino Uno (Rev3)
  R2 = Resistor [tolerance=±5% resistance=220 package=THT]
  R3 = Resistor [tolerance=±5% resistance=220 package=THT]
  R4 = Resistor [tolerance=±5% resistance=220 package=THT]
  U1 = LCD-16X2 [package=lcd-16x2]
  LED3 = smd LED [color="Red (633nm)" package="0805 [SMD]"]
  LED4 = smd LED [color="Red (633nm)" package="0805 [SMD]"]
  S1 = Pushbutton [package="[SMD]"]
  S2 = Pushbutton [package="[SMD]"]
  S3 = Pushbutton [package="[SMD]"]
  S4 = Pushbutton [package="[SMD]"]
  LED6 = smd LED [color="Red (633nm)" package="0805 [SMD]"]
  LED7 = smd LED [color="Red (633nm)" package="0805 [SMD]"]
  R5 = Trimmer Potentiometer [maximum_resistance=10kΩ package=THT]

nets:
  N1: R1.Pin_0, LED6.anode
  N2: R1.Pin_1, Part1.D10_PWM/SS
  N3: Part1.A0, S1.Pin_3, S1.Pin_4
  N4: Part1.A1, S2.Pin_3, S2.Pin_4
  N5: Part1.A2, S3.Pin_1, S3.Pin_2
  N6: Part1.A3, S4.Pin_1, S4.Pin_2
  N7: Part1.D8, U1.RS
  N8: Part1.D9_PWM, U1.E
  N9: Part1.D11_PWM/MOSI, R3.Pin_1
  N10: Part1.D12/MISO, R4.Pin_0
  N11: Part1.D13/SCK, R2.Pin_0
  GND: Part1.GND, U1.VSS, U1.R_W, U1.K, LED3.cathode, LED4.cathode, S1.Pin_1, S1.Pin_2, S2.Pin_1, S2.Pin_2, S3.Pin_3, S3.Pin_4, S4.Pin_3, S4.Pin_4, LED6.cathode, LED7.cathode, R5.leg1
  N12: Part1.D4, U1.DB4
  N13: Part1.D5_PWM, U1.DB5
  N14: Part1.D6_PWM, U1.DB6
  N15: Part1.D7, U1.DB7
  5V: Part1.5V, U1.VDD, U1.A, R5.leg2
  N16: R2.Pin_1, LED3.anode
  N17: R3.Pin_0, LED7.anode
  N18: R4.Pin_1, LED4.anode
  N19: U1.VO, R5.wiper
